# Fritzing sketch ups_board (saved by Fritzing 0.8.3b)
breadboards: 1

parts:
  D1 = Rectifier Diode [part_number=1N4007 package="300 mil [THT]"]
  D2 = Rectifier Diode [part_number=1N4007 package="300 mil [THT]"]
  D3 = Rectifier Diode [part_number=1N4007 package="300 mil [THT]"]
  D4 = Rectifier Diode [part_number=1N4007 package="300 mil [THT]"]
  R1 = Resistor [tolerance=±5% resistance=2.2k power=2W package=THT]
  D5 = Rectifier Diode [part_number=1N4001 package="300 mil [THT]"]
  D6 = Rectifier Diode [part_number=1N4001 package="300 mil [THT]"]
  R2 = Resistor [tolerance=±5% resistance=4.7 package=THT]
  12V_Li-Ion_Battery = Screw terminal - 2 pins [package=THT]
  R3 = Resistor [tolerance=±5% resistance=4.7k package=THT]
  J2_-_12V_DC_out = Screw terminal - 2 pins [package=THT]
  LED2 = LED - 5mm [color="Green (565nm)" package="5 mm [THT]"]
  R4 = Resistor [tolerance=±5% resistance=1k package=THT]
  LED3 = LED - 5mm [color="Red (633nm)" package="5 mm [THT]"]
  IC1 = IC, DIP package, 8 pins [chip_label=IC741]
  Q2 = NPN-Transistor [package="TO92 [THT]"]
  Q3 = PNP-Transistor [package="TO92 [THT]"]
  U1 = Voltage Regulator - 5V [package="TO220 [THT]"]
  VCC1 = Battery block 9V
  R5 = TRIMPOT [part_number="100k preset" package=trimpot_pth_s3_lock]
  R6 = Resistor [tolerance=±5% resistance=1k package=THT]
  R7 = TRIMPOT [part_number="10k preset" package=trimpot_pth_s3_lock]
  U2 = DIODE-ZENER [package=sod-323]
  D7 = Rectifier Diode [part_number=1N4001 package="300 mil [THT]"]
  R8 = Resistor [tolerance=±5% resistance=10k package=THT]

nets:
  N1: D1.cathode, D4.anode
  N2: D1.anode, D3.cathode
  N3: D2.cathode, D3.anode
  N4: D2.anode, R1.Pin_0, U1.GND
  N5: D4.cathode, R2.Pin_1, R3.Pin_1, J2_-_12V_DC_out.pin2, IC1.pin4, Q2.E, VCC1.-, R5.CCW, R7.CCW, U2.A
  N6: R1.Pin_1, D6.anode, Q3.E, U1.output_voltage
  N7: D5.cathode, J2_-_12V_DC_out.pin1, D7.cathode
  N8: D5.anode, D6.cathode
  N9: R2.Pin_0, 12V_Li-Ion_Battery.pin2
  N10: 12V_Li-Ion_Battery.pin1, Q2.B, D7.anode
  N11: R3.Pin_0, LED2.cathode
  N12: LED2.anode, R4.Pin_1, IC1.pin6
  N13: R4.Pin_0, LED3.cathode
  N14: LED3.anode, Q3.B
  N15: IC1.pin2, Q2.C, U2.C
  N16: IC1.pin3, R6.Pin_1, R8.Pin_0
  N17: Q3.C, R7.CW
  N18: U1.input_voltage, VCC1.+
  N19: R5.WIPER, R5.CW, R6.Pin_0
  N20: R7.WIPER, R8.Pin_1
