# Fritzing sketch x (saved by Fritzing 0.8.3b)
breadboards: 1

parts:
  VCC1 = Battery
  D1 = Rectifier Diode [part_number=1N4007 package="300 mil [THT]"]
  D2 = Rectifier Diode [part_number=1N4007 package="300 mil [THT]"]
  D3 = Rectifier Diode [part_number=1N4007 package="300 mil [THT]"]
  D4 = Rectifier Diode [part_number=1N4007 package="300 mil [THT]"]
  R1 = Resistor [tolerance=±5% resistance=2.2k power=2W package=THT]
  D5 = Rectifier Diode [part_number=1N4001 package="300 mil [THT]"]
  D6 = Rectifier Diode [part_number=1N4001 package="300 mil [THT]"]  # not connected
  U1 = Voltage Regulator - 5V [part_number=MC78T12 package="TO220 [THT]"]
  Q1 = NPN-Transistor [package="TO92 [THT]"]

nets:
  N1: VCC1.+, U1.input_voltage
  N2: D1.cathode, D4.anode
  N3: D1.anode, D3.cathode
  N4: D2.cathode, D3.anode
  N5: D2.anode, R1.Pin_0, U1.GND
  N6: R1.Pin_1, U1.output_voltage
  N7: D5.cathode, Q1.E
