# Fritzing sketch ups (saved by Fritzing 0.8.3b)
breadboards: 1

parts:
  19V_DC = Screw terminal - 2 pins [package=THT]
  C1 = Ceramic Capacitor [capacitance=100nF package="100 mil [THT, multilayer]"]
  U1 = Voltage Regulator - Variable [package="TO220 [THT]"]
  R2 = Trimmer Potentiometer [maximum_resistance=10kΩ package=THT]
  C2 = Ceramic Capacitor [capacitance=100nF package="100 mil [THT, multilayer]"]
  R3 = Resistor [tolerance=±5% resistance=220 package=THT]

nets:
  N1: 19V_DC.pin1, C1.1, U1.IN
  GND: 19V_DC.pin2, C1.0, U1.ADJ, R2.leg1, C2.1, R3.Pin_1
  N2: U1.OUT, C2.0
  N3: R2.wiper, R2.leg2, R3.Pin_0
